# Fritzing sketch tplus doorlock (saved by Fritzing 0.9.3b)

parts:
  U1 = NodeMCU V3.0
  VCC1 = Battery
  S1 = Momentary Switch [package=ksa_sealed_tac_switch]  # not connected
  부품1 = Solid State High Level Relay Module [package=relay]  # not connected

nets:
  N1: U1.Vin, VCC1.+
  N2: U1.GND, VCC1.-

custom parts:
  NodeMCU V3.0: ESP8266 based NodeMCU
  Solid State High Level Relay Module: 5V Omron solid state relay 240V 2A output with resistance fuse.
