# Fritzing sketch tplus-switch (saved by Fritzing 0.9.3b)

parts:
  U1 = NodeMCU V3.0
  HLK-PM1 = HLK-PM01
  부품1 = Solid State High Level Relay Module [package=relay]
  LED1 = LEDs [package=led10mm]
  Power_plug1 = Power plug

nets:
  N1: U1.D4, 부품1.CH1
  N2: U1.GND, HLK-PM1.-Vo, 부품1.DC-
  N3: U1.Vin, HLK-PM1.+Vo, 부품1.DC+
  N4: HLK-PM1.AC#0, 부품1.B1, Power_plug1.VCC
  N5: HLK-PM1.AC#1, LED1.A, Power_plug1.GND
  N6: 부품1.A1, LED1.C

custom parts:
  NodeMCU V3.0: ESP8266 based NodeMCU
  Solid State High Level Relay Module: 5V Omron solid state relay 240V 2A output with resistance fuse.
